# Fritzing sketch filter (saved by Fritzing 0.9.3b)
breadboards: 1

parts:
  BeagleBone1 = BeagleBone Black
  R1 = Trimmer Potentiometer [maximum_resistance=10kΩ package=THT]
  C1 = Ceramic Capacitor [capacitance=0.22µF package="100 mil [THT, multilayer]"]

nets:
  N1: BeagleBone1.no_name_yet#1, C1.1
  N2: BeagleBone1.no_name_yet#31, R1.wiper
  N3: R1.leg1, C1.0

notes:
  +
  -
  P9
  P8

custom parts:
  BeagleBone Black: BeagleBone Black rev. A5B
