# Fritzing sketch neo (saved by Fritzing 0.9.3b)
breadboards: 1

parts:
  BeagleBone1 = BeagleBone Black
  Part1 = 24 NeoPixel Ring [part_number=1586]

nets:
  N1: BeagleBone1.no_name_yet#1, Part1.GND
  N2: BeagleBone1.no_name_yet#3, Part1.VDD
  N3: BeagleBone1.no_name_yet#29, Part1.IN

notes:
  +
  -
  P9
  P8

custom parts:
  BeagleBone Black: BeagleBone Black rev. A5B
  24 NeoPixel Ring: 24 ultra bright smart LED NeoPixels are arranged in a circle with 2.6" (66mm) outer diameter. The rings are 'chainable' - connect the output pin of one to the input pin of another. Use only one microcontroller pin to control as many as you can chain together! Each LED is addressable as the driver chip is inside the LED. Each one has ~18mA constant current drive so the color will be very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
